# Fritzing sketch Mide_la_temperatura_y_enciende_un_led_rojo-azul_segun_esta (saved by Fritzing 0.9.2b)
breadboards: 1

parts:
  Parte1 = Arduino Uno (Rev3)
  LED1 = RGB LED (com. anode, rbg) [package="5 mm [THT]"]
  R1 = Resistor [tolerance=±5% resistance=220 package="2010 [SMD]"]
  R2 = Resistor [tolerance=±5% resistance=220 package="2010 [SMD]"]
  T1 = LM35 Temperature Sensor [package="TO92 [THT]"]

nets:
  N1: Parte1.A0, T1.Vout
  N2: Parte1.D5_PWM, R1.Pin_1
  N3: Parte1.D6_PWM, R2.Pin_1
  N4: Parte1.5V, T1.+Vs
  GND: Parte1.GND, T1.GND
  N5: LED1.red_cathode, R2.Pin_0
  N6: LED1.blue_cathode, R1.Pin_0

// code stored in the sketch: Mide la temperatura y enciende un led rojo-azul segun esta.ino
const int sensor = 0;
  const int rojo = 5;
  const int azul = 6 ;
  int brillo; 
  long miliVolts; // porque las multiplicaciones que haremos tendrán muchos números que no cabran en int
  long temperatura;

  void setup() {
  Serial.begin(9600); // para empezar la comunicación tú-arduino 
  pinMode(rojo, OUTPUT);
  pinMode(azul, OUTPUT);
  }

  void loop() {
 
  miliVolts = (analogRead(sensor) * 5000L) / 1023; //lee el sensor y convierte la señal analógica(0-1023) a miliVoltios(0-5000). Se pone L para que arduino sepa que es una variable Long
  temperatura = miliVolts/10; //Pasamos de miliVolts a ºC
  
  Serial.print("La temperatura es: ");
  Serial.print(temperatura);
  Serial.print(" grados.\n");
  delay(200);
  
  brillo = map(temperatura, 10,40,0,255);  //Cambia la escala de los datos (0,255) el rango de señal de analog write para encender un led
  brillo = constrain(brillo, 0,255); //limita los valores a 0 y 255, porque si temperatura =0 => brillo<0
  
  analogWrite(rojo, brillo);
  analogWrite(azul, 255-brillo);
  
  
}
